# Fritzing sketch PCM2704_HPA_Case (saved by Fritzing 0.9.3b)
perfboards: 2

parts:
  U1 = Mini-USB _B_ connector with 5th pin broken out. [package=usb-minib]  # not connected
  J1 = female pin header, 2 pins [form="♀ (female)"]
  J2 = female pin header, 2 pins [form="♀ (female)"]
  J3 = female pin header, 2 pins [form="♀ (female)"]
  J4 = female pin header, 2 pins [form="♀ (female)"]
  J5 = female pin header, 3 pins [form="♀ (female)"]
  J6 = female pin header, 3 pins [form="♀ (female)"]
  J7 = female pin header, 3 pins [form="♀ (female)"]  # not connected
  J8 = female pin header, 2 pins [form="♀ (female)"]
  J9 = female pin header, 2 pins [form="♀ (female)"]
  J10 = female pin header, 2 pins [form="♀ (female)"]
  J11 = female pin header, 2 pins [form="♀ (female)"]
  J12 = female pin header, 3 pins [form="♀ (female)"]
  Power_plug1 = Power plug
  Power_plug2 = Power plug
  S1 = Taiway 100-SP-X-T1 SPDT Miniature Toggle Switch [part_number=100-SP-X-T1-0-0-B1-M1 package=THT]
  S2 = Taiway 100-SP-X-T1 SPDT Miniature Toggle Switch [part_number=100-SP-X-T1-0-0-B1-M1 package=THT]
  LED1 = LED - 5mm [color="Green (570nm)" package="5 mm [THT]"]
  LED2 = LED - 5mm [color="Blue (525nm)" package="5 mm [THT]"]
  S3 = Taiway 100-SP-X-T1 SPDT Miniature Toggle Switch [part_number=100-SP-X-T1-0-0-B1-M1 package=THT]
  S4 = Taiway 100-SP-X-T1 SPDT Miniature Toggle Switch [part_number=100-SP-X-T1-0-0-B1-M1 package=THT]
  R1 = Rotary Potentiometer (Small) [maximum_resistance=10kΩ package=THT]
  R2 = Rotary Potentiometer (Small) [maximum_resistance=10kΩ package=THT]
  TRS1 = Audio Jack (TRS) 3.5mm [package="4Ucon 08780 [THT]"]
  JP1 = RCA [package=rca_lock]
  JP2 = RCA [package=rca_lock]
  JP3 = RCA [package=rca_lock]
  JP4 = RCA [package=rca_lock]
  JP5 = RCA [package=rca_lock]
  JP6 = RCA [package=rca_lock]
  J13 = female pin header, 2 pins [form="♀ (female)"]
  J14 = female pin header, 2 pins [form="♀ (female)"]

nets:
  N1: J1.pin1, JP1.SHELL
  N2: J1.pin2, JP1.PIN
  N3: J2.pin1, J8.pin1, R1.leg1, JP4.SHELL, JP5.SHELL
  N4: J3.pin1, JP2.SHELL
  N5: J3.pin2, JP2.PIN
  N6: J4.pin1, R2.leg1, JP3.SHELL, JP6.SHELL
  N7: J4.pin2, S4.L2
  N8: J5.pin1, S2.L1
  GND: J5.pin2, Power_plug1.GND, Power_plug2.GND
  N9: J5.pin3, S1.COM
  N10: J6.pin1, J12.pin1
  N11: J6.pin2, J12.pin2
  N12: J6.pin3, J12.pin3
  N13: J9.pin2, R2.wiper
  N14: J10.pin1, J11.pin1, J11.pin2, TRS1.Tip
  N15: J10.pin2, TRS1.Ring
  N16: Power_plug1.VCC, S1.L2
  N17: Power_plug2.VCC, S2.L2
  N18: LED1.cathode, J14.pin2
  N19: LED1.anode, J14.pin1
  N20: LED2.cathode, J13.pin1
  N21: LED2.anode, J13.pin2
  N22: S3.COM, R1.leg2
  N23: S3.L1, JP4.PIN, JP5.PIN
  N24: S4.COM, R2.leg2
  N25: S4.L1, JP3.PIN, JP6.PIN

notes:
  DPDT
  Dual POT 10kΩ/A
  6.3Φ
  Stereo
  HeadPhone OUT
  DAC
  LINE OUT
  AUX IN
  AUX THRU
  POWER IN
  +9V / -9V
  Mini USB
  PCM2904 HPA
  ケース内配線図
  2019.12.26
