# Fritzing sketch PCM2704_LineAmp (saved by Fritzing 0.9.3b)
breadboards: 2

parts:
  U1 = mystery part, 28 pins [chip_label=PCM2704]
  R2 = Resistor [tolerance=±5% resistance=100k package=THT]
  R3 = Resistor [tolerance=±5% resistance=100k package=THT]
  C1 = Film/Foil Capacitor [capacitance=100nF voltage=35V package="5mm [THT, pp]"]
  C2 = Film/Foil Capacitor [capacitance=100nF voltage=35V package="5mm [THT, pp]"]
  IC1 = Dual Op-Amp [package=dip08]
  C3 = Ceramic Capacitor [capacitance=100nF package="100 mil [THT, multilayer]"]
  C4 = Ceramic Capacitor [capacitance=100nF package="100 mil [THT, multilayer]"]
  R4 = Resistor [tolerance=±5% resistance=3.3k package=THT]
  LED1 = LED - 3mm [color="Green (570nm)" package="3 mm [THT]"]

nets:
  N1: U1.pin7, C1.-
  N2: U1.pin9, R2.Pin_1, R3.Pin_1, C3.0, C4.1
  N3: U1.pin11, C2.-
  N4: U1.pin22, LED1.cathode
  N5: U1.pin23, U1.pin24, R4.Pin_0
  N6: R2.Pin_0, C1.+, IC1.B_+IN
  N7: R3.Pin_0, C2.+, IC1.A_+IN
  N8: IC1.A_OUT, IC1.A_-IN
  N9: IC1.A_V-, C4.0
  N10: IC1.B_-IN, IC1.B_OUT
  N11: IC1.A_V+, C3.1
  N12: R4.Pin_1, LED1.anode

notes:
  GND
  +9V
  -9V
  GND
  OUT L
  OUT R
