# Fritzing sketch PCM2704_LineAmp_Snubber (saved by Fritzing 0.9.3b)
breadboards: 2

parts:
  U1 = mystery part, 28 pins [chip_label=PCM2704]
  R2 = Resistor [tolerance=±5% resistance=330 package=THT]
  R3 = Resistor [tolerance=±5% resistance=330 package=THT]
  IC1 = Dual Op-Amp [package=dip08]
  C3 = Ceramic Capacitor [capacitance=100nF package="100 mil [THT, multilayer]"]
  C4 = Ceramic Capacitor [capacitance=100nF package="100 mil [THT, multilayer]"]
  R4 = Resistor [tolerance=±5% resistance=3.3k package=THT]
  C5 = Electrolytic Capacitor [capacitance=1µF package="100 mil [THT, electrolytic]"]
  C6 = Electrolytic Capacitor [capacitance=1µF package="100 mil [THT, electrolytic]"]
  R5 = Resistor [tolerance=±5% resistance=15 package=THT]
  C7 = Ceramic Capacitor [capacitance=100nF package="100 mil [THT, multilayer]"]
  R6 = Resistor [tolerance=±5% resistance=15 package=THT]
  C8 = Ceramic Capacitor [capacitance=100nF package="100 mil [THT, multilayer]"]
  LED1 = LED - 3mm [color="Green (570nm)" package="3 mm [THT]"]
  R7 = Resistor [tolerance=±5% resistance=10k package=THT]
  R8 = Resistor [tolerance=±5% resistance=10k package=THT]

nets:
  N1: U1.pin7, C5.+, C8.0, R7.Pin_0
  N2: U1.pin9, R2.Pin_1, R3.Pin_1, C3.0, C4.1, R5.Pin_1, R6.Pin_1, R7.Pin_1, R8.Pin_1
  N3: U1.pin11, C6.+, C7.0, R8.Pin_0
  N4: U1.pin22, LED1.cathode
  N5: U1.pin23, U1.pin24, R4.Pin_0
  N6: R2.Pin_0, IC1.B_+IN, C5.-
  N7: R3.Pin_0, IC1.A_+IN, C6.-
  N8: IC1.A_OUT, IC1.A_-IN
  N9: IC1.A_V-, C4.0
  N10: IC1.B_-IN, IC1.B_OUT
  N11: IC1.A_V+, C3.1
  N12: R4.Pin_1, LED1.anode
  N13: R5.Pin_0, C7.1
  N14: R6.Pin_0, C8.1

notes:
  GND
  +9V
  -9V
  GND
  OUT L
  OUT R
  100uF x 2
  0.022uF x2
